// Logisim project Project2.circ as structural Verilog: 7 circuits, main circuit logic
module main (
);

  wire clock_1_out, counter_1_l0, counter_1_l1, counter_1_l2, counter_1_l3, counter_2_is_nine, counter_2_l0,
       counter_2_l1, counter_2_l2, counter_2_l3, four_bit_adder_1_cout, four_bit_adder_1_out1,
       four_bit_adder_1_out2, four_bit_adder_1_out3, four_bit_adder_1_out4, logic_1_a, logic_1_b, logic_1_c,
       logic_1_d, logic_1_e, logic_1_f, logic_1_g, logic_2_a, logic_2_b, logic_2_c, logic_2_d, logic_2_e,
       logic_2_f, logic_2_g, logic_3_a, logic_3_b, logic_3_c, logic_3_d, logic_3_e, logic_3_f, logic_3_g,
       logic_4_a, logic_4_b, logic_4_c, logic_4_d, logic_4_e, logic_4_f, logic_4_g, nias_chip_1_a0,
       nias_chip_1_b0, nias_chip_1_b1, nias_chip_1_b2, nias_chip_1_b3;

  \logic  logic_1 (
    .a(logic_1_a), .b(logic_1_b), .c(logic_1_c), .d(logic_1_d), .e(logic_1_e), .f(logic_1_f), .g(logic_1_g),
    .w(counter_1_l0), .x(counter_1_l1), .y(counter_1_l2), .z(counter_1_l3));
  _7_Segment_Display u_7_segment_display_1 (
    .g(logic_1_g), .f(logic_1_f), .a(logic_1_a), .b(logic_1_b), .e(logic_1_e), .d(logic_1_d), .c(logic_1_c));  // open: dp
  \logic  logic_2 (
    .a(logic_2_a), .b(logic_2_b), .c(logic_2_c), .d(logic_2_d), .e(logic_2_e), .f(logic_2_f), .g(logic_2_g),
    .w(counter_2_l0), .x(counter_2_l1), .y(counter_2_l2), .z(counter_2_l3));
  Clock clock_1 (.out(clock_1_out));
  counter counter_1 (
    .L0(counter_1_l0), .L1(counter_1_l1), .L2(counter_1_l2), .L3(counter_1_l3), .Clock(counter_2_is_nine));  // open: IS_NINE
  _7_Segment_Display u_7_segment_display_2 (
    .g(logic_2_g), .f(logic_2_f), .a(logic_2_a), .b(logic_2_b), .e(logic_2_e), .d(logic_2_d), .c(logic_2_c));  // open: dp
  \logic  logic_3 (
    .a(logic_3_a), .b(logic_3_b), .c(logic_3_c), .d(logic_3_d), .e(logic_3_e), .f(logic_3_f), .g(logic_3_g),
    .w(nias_chip_1_a0), .x(1'b0), .y(1'b0), .z(1'b0));
  counter counter_2 (
    .L0(counter_2_l0), .L1(counter_2_l1), .L2(counter_2_l2), .L3(counter_2_l3), .Clock(clock_1_out),
    .IS_NINE(counter_2_is_nine));
  _7_Segment_Display u_7_segment_display_3 (
    .g(logic_3_g), .f(logic_3_f), .a(logic_3_a), .b(logic_3_b), .e(logic_3_e), .d(logic_3_d), .c(logic_3_c));  // open: dp
  \logic  logic_4 (
    .a(logic_4_a), .b(logic_4_b), .c(logic_4_c), .d(logic_4_d), .e(logic_4_e), .f(logic_4_f), .g(logic_4_g),
    .w(nias_chip_1_b0), .x(nias_chip_1_b1), .y(nias_chip_1_b2), .z(nias_chip_1_b3));
  four_bit_adder four_bit_adder_1 (
    .ina1(counter_2_l0), .ina2(counter_2_l1), .ina3(counter_2_l2), .ina4(counter_2_l3), .inb1(counter_1_l0),
    .inb2(counter_1_l1), .inb3(counter_1_l2), .inb4(counter_1_l3), .cin(1'b0), .out1(four_bit_adder_1_out1),
    .out2(four_bit_adder_1_out2), .out3(four_bit_adder_1_out3), .out4(four_bit_adder_1_out4),
    .cout(four_bit_adder_1_cout));
  _7_Segment_Display u_7_segment_display_4 (
    .g(logic_4_g), .f(logic_4_f), .a(logic_4_a), .b(logic_4_b), .e(logic_4_e), .d(logic_4_d), .c(logic_4_c));  // open: dp
  nias_chip nias_chip_1 (
    .s4(four_bit_adder_1_cout), .s3(four_bit_adder_1_out4), .s2(four_bit_adder_1_out3),
    .s1(four_bit_adder_1_out2), .s0(four_bit_adder_1_out1), .a0(nias_chip_1_a0), .b3(nias_chip_1_b3),
    .b2(nias_chip_1_b2), .b1(nias_chip_1_b1), .b0(nias_chip_1_b0));
endmodule

module \logic  (
  input  z,
  input  y,
  input  x,
  input  w,
  output b,
  output a,
  output f,
  output g,
  output e,
  output d,
  output c
);

  wire and_1_out, and_2_out, and_3_out, and_4_out, nand_1_out, nand_2_out, nand_3_out, nor_1_out, not_1_out,
       not_2_out, not_3_out, not_4_out, not_5_out, or_1_out, or_2_out, or_3_out, or_4_out, xnor_1_out,
       xor_1_out;

  and and_1 (and_1_out, y, w);
  nand nand_1 (nand_1_out, x, w);
  not not_1 (not_1_out, z);
  nand nand_2 (nand_2_out, y, w);
  or or_1 (or_1_out, y, w);
  not not_2 (not_2_out, x);
  nand nand_3 (nand_3_out, x, w);
  or or_2 (or_2_out, x, w);
  not not_3 (not_3_out, x);
  or or_3 (or_3_out, x, w, y);
  or or_4 (or_4_out, z, xnor_1_out);
  xnor xnor_1 (xnor_1_out, x, and_1_out);
  and and_2 (and_2_out, y, not_4_out);
  not not_4 (not_4_out, x);
  and and_3 (and_3_out, y, nand_1_out);
  nor nor_1 (nor_1_out, w, x);
  not not_5 (not_5_out, w);
  and and_4 (and_4_out, not_5_out, x);
  xor xor_1 (xor_1_out, x, y);
  nand nand_4 (a, not_1_out, nand_2_out, or_1_out, not_2_out);
  nand nand_5 (b, y, nand_3_out, or_2_out);
  or or_5 (c, y, not_3_out, w);
  nand nand_6 (d, or_3_out, or_4_out);
  nor nor_2 (e, w, and_2_out);
  or or_6 (f, z, and_3_out, nor_1_out);
  or or_7 (g, z, and_4_out, xor_1_out);
endmodule

module counter (
  input  Clock,
  output L0,
  output L1,
  output L2,
  output L3,
  output IS_NINE
);

  wire and_2_out, and_3_out, and_4_out, and_5_out, and_6_out, and_7_out, and_8_out, D1_qn, D2_qn, D3_qn,
       D4_qn, or_1_out, or_2_out, or_3_out;

  and and_1 (IS_NINE, L3, D2_qn, D3_qn, L0);
  and and_2 (and_2_out, L3, D4_qn);
  and and_3 (and_3_out, L2, L1, L0);
  and and_4 (and_4_out, L2, D3_qn);
  and and_5 (and_5_out, L2, D4_qn);
  and and_6 (and_6_out, D2_qn, L1, L0);
  and and_7 (and_7_out, L1, D4_qn);
  and and_8 (and_8_out, D1_qn, D3_qn, L0);
  or or_1 (or_1_out, and_2_out, and_3_out);
  or or_2 (or_2_out, and_4_out, and_5_out, and_6_out);
  or or_3 (or_3_out, and_7_out, and_8_out);
  D_Flip_Flop #(.trigger("falling")) D1 (.clk(Clock), .D(or_1_out), .Q(L3), .Qn(D1_qn));  // open: preset, en, reset
  D_Flip_Flop #(.trigger("falling")) D2 (.clk(Clock), .D(or_2_out), .Q(L2), .Qn(D2_qn));  // open: preset, en, reset
  D_Flip_Flop #(.trigger("falling")) D3 (.clk(Clock), .D(or_3_out), .Q(L1), .Qn(D3_qn));  // open: preset, en, reset
  D_Flip_Flop #(.trigger("falling")) D4 (.clk(Clock), .D(D4_qn), .Q(L0), .Qn(D4_qn));  // open: preset, en, reset
endmodule

module one_bit_adder (
  input  a,
  input  b,
  input  cin,
  output cout,
  output sum
);

  wire and_1_out, and_2_out, and_3_out, and_4_out, or_1_out, xor_1_out;

  or or_1 (or_1_out, cin, 1'b0);
  and and_1 (and_1_out, or_1_out, b, a);
  ExactlyOne xor_1 (.out(xor_1_out), .in0(or_1_out), .in1(b), .in2(a));
  or or_2 (sum, and_1_out, xor_1_out);
  and and_2 (and_2_out, a, b);
  and and_3 (and_3_out, b, or_1_out);
  and and_4 (and_4_out, a, or_1_out);
  or or_3 (cout, and_2_out, and_3_out, and_4_out);
endmodule

module two_bit_adder (
  input  ina1,
  input  ina2,
  input  inb1,
  input  inb2,
  input  cin,
  output ou1,
  output out2,
  output cout
);

  wire one_bit_adder_1_cout, or_1_out;

  or or_1 (or_1_out, cin, 1'b0);
  one_bit_adder one_bit_adder_1 (.a(ina1), .b(inb1), .cin(or_1_out), .cout(one_bit_adder_1_cout), .sum(ou1));
  one_bit_adder one_bit_adder_2 (.a(ina2), .b(inb2), .cin(one_bit_adder_1_cout), .cout(cout), .sum(out2));
endmodule

module four_bit_adder (
  input  ina1,
  input  ina2,
  input  ina3,
  input  ina4,
  input  inb1,
  input  inb2,
  input  inb3,
  input  inb4,
  input  cin,
  output out1,
  output out2,
  output out3,
  output out4,
  output cout
);

  wire two_bit_adder_1_cout;

  two_bit_adder two_bit_adder_1 (
    .ina1(ina1), .ina2(ina2), .inb1(inb1), .inb2(inb2), .cin(cin), .ou1(out1), .out2(out2),
    .cout(two_bit_adder_1_cout));
  two_bit_adder two_bit_adder_2 (
    .ina1(ina3), .ina2(ina4), .inb1(inb3), .inb2(inb4), .cin(two_bit_adder_1_cout), .ou1(out3), .out2(out4),
    .cout(cout));
endmodule

module nias_chip (
  input  s4,
  input  s3,
  input  s2,
  input  s1,
  input  s0,
  output a0,
  output b3,
  output b2,
  output b1,
  output b0
);

  wire and_1_out, and_2_out, and_3_out, and_4_out, and_5_out, and_6_out, and_7_out, and_8_out, and_9_out,
       and_10_out, not_1_out, not_2_out, not_3_out, not_4_out, not_5_out, not_6_out, not_7_out, not_8_out;

  and and_1 (and_1_out, s3, s1);
  and and_2 (and_2_out, s3, s2);
  not not_1 (not_1_out, s2);
  not not_2 (not_2_out, s1);
  not not_3 (not_3_out, s3);
  not not_4 (not_4_out, s1);
  not not_5 (not_5_out, s4);
  not not_6 (not_6_out, s3);
  not not_7 (not_7_out, s1);
  not not_8 (not_8_out, s1);
  or or_1 (a0, and_1_out, and_2_out, s4);
  and and_3 (and_3_out, s3, not_1_out, not_2_out);
  and and_4 (and_4_out, s4, s1);
  and and_5 (and_5_out, not_3_out, s2);
  and and_6 (and_6_out, s2, s1);
  and and_7 (and_7_out, s4, not_4_out);
  and and_8 (and_8_out, not_5_out, not_6_out, s1);
  and and_9 (and_9_out, s3, s2, not_7_out);
  and and_10 (and_10_out, s4, not_8_out);
  or or_2 (b3, and_3_out, and_4_out);
  or or_3 (b2, and_5_out, and_6_out, and_7_out);
  or or_4 (b1, and_8_out, and_9_out, and_10_out);

  assign b0 = s0;
endmodule
